// Digital circuit 3 bit Program Counter.dig as structural Verilog
module _3_bit_Program_Counter (
  input  [2:0] I_2_0,
  input  CLK,
  output [2:0] O_2_0
);

  _1_bit_Reg _1_bit_reg_1 (.Din(I_2_0[2]), .Sel(1'b1), .CLK(CLK), .Dout(O_2_0[2]));
  _1_bit_Reg _1_bit_reg_2 (.Din(I_2_0[1]), .Sel(1'b1), .CLK(CLK), .Dout(O_2_0[1]));
  _1_bit_Reg _1_bit_reg_3 (.Din(I_2_0[0]), .Sel(1'b1), .CLK(CLK), .Dout(O_2_0[0]));

  // Other names for the same wires on the sheet: I0 = I_2_0[0]; I1 = I_2_0[1]; I2 = I_2_0[2]; O0 = O_2_0[0];
  //   O1 = O_2_0[1]; O2 = O_2_0[2]
endmodule
