// Digital circuit 3x5 Reg Set.dig as structural Verilog
module _3x5_Reg_Set (
  input  [4:0] WRD_4_0,
  input  [1:0] WR_1_0,
  input  REG_EN,
  input  CLK,
  input  [1:0] Ra_1_0,
  input  [1:0] Rb_1_0,
  output [4:0] A_4_0,
  output [4:0] B_4_0
);

  wire E0, E1, E2, R0, R1, R2;
  wire [4:0] D0, D1, D2;

  and and_1 (R0, REG_EN, E0);
  and and_2 (R1, REG_EN, E1);
  Decoder #(.Selector_Bits(2)) decoder_1 (.sel(WR_1_0), .out_0(E0), .out_1(E1), .out_2(E2));  // open: out_3
  and and_3 (R2, REG_EN, E2);
  _5_bit_Reg _5_bit_reg_1 (.Din_4_0(WRD_4_0), .Sel(R2), .CLK(CLK), .Dout(D2));
  _5_bit_Reg _5_bit_reg_2 (.Din_4_0(WRD_4_0), .Sel(R1), .CLK(CLK), .Dout(D1));
  _5_bit_Reg _5_bit_reg_3 (.Din_4_0(WRD_4_0), .Sel(R0), .CLK(CLK), .Dout(D0));
  Multiplexer #(.Selector_Bits(2), .Bits(5)) multiplexer_1 (
    .sel(Ra_1_0), .in_0(D0), .in_1(D1), .in_2(D2), .in_3({5{1'b0}}), .out(A_4_0));
  Multiplexer #(.Selector_Bits(2), .Bits(5)) multiplexer_2 (
    .sel(Rb_1_0), .in_0(D0), .in_1(D1), .in_2(D2), .in_3({5{1'b0}}), .out(B_4_0));

  // Other names for the same wires on the sheet: RE = REG_EN
endmodule
