// Digital circuit 5 bit ALU.dig as structural Verilog
module _5_bit_ALU (
  input  [4:0] A_4_0,
  input  [4:0] B_4_0,
  input  [1:0] OP_1_0,
  output [4:0] R_4_0
);

  wire [4:0] R_Add, R_ROL, R_XOR;

  _5_bit_XOR _5_bit_xor_1 (.A_4_0(A_4_0), .B_4_0(B_4_0), .R_4_0(R_XOR));
  _5_bit_Adder _5_bit_adder_1 (.A_4_0(A_4_0), .B_4_0(B_4_0), .R_4_0(R_Add));  // open: Cout
  _5_bit_Left_Rotator _5_bit_left_rotator_1 (.A_4_0(A_4_0), .B_4_0(B_4_0), .R_4_0(R_ROL));
  Multiplexer #(.Selector_Bits(2), .Bits(5)) multiplexer_1 (
    .sel(OP_1_0), .in_0(R_XOR), .in_1(R_Add), .in_2(R_ROL), .in_3({5{1'b0}}), .out(R_4_0));

  // Other names for the same wires on the sheet: A[4:0] = A_4_0; B[4:0] = B_4_0; OP[1:0] = OP_1_0
endmodule
