// Digital circuit 5 bit Adder.dig as structural Verilog
module _5_bit_Adder (
  input  [4:0] A_4_0,
  input  [4:0] B_4_0,
  output [4:0] R_4_0,
  output Cout
);

  wire full_adder_2_cout, full_adder_3_cout, full_adder_4_cout, full_adder_5_cout;

  Full_Adder full_adder_1 (.Y(B_4_0[4]), .X(A_4_0[4]), .Cin(full_adder_2_cout), .Cout(Cout), .S(R_4_0[4]));
  Full_Adder full_adder_2 (.Y(B_4_0[3]), .X(A_4_0[3]), .Cin(full_adder_3_cout), .Cout(full_adder_2_cout), .S(R_4_0[3]));
  Full_Adder full_adder_3 (.Y(B_4_0[2]), .X(A_4_0[2]), .Cin(full_adder_4_cout), .Cout(full_adder_3_cout), .S(R_4_0[2]));
  Full_Adder full_adder_4 (.Y(B_4_0[1]), .X(A_4_0[1]), .Cin(full_adder_5_cout), .Cout(full_adder_4_cout), .S(R_4_0[1]));
  Full_Adder full_adder_5 (.Y(B_4_0[0]), .X(A_4_0[0]), .Cin(1'b0), .Cout(full_adder_5_cout), .S(R_4_0[0]));
endmodule
