// Digital circuit 5 bit Left Rotator.dig as structural Verilog
module _5_bit_Left_Rotator (
  input  [4:0] A_4_0,
  input  [4:0] B_4_0,
  output [4:0] R_4_0
);

  Multiplexer #(.Selector_Bits(5)) multiplexer_1 (
    .sel(B_4_0), .in_0(A_4_0[4]), .in_1(A_4_0[3]), .in_2(A_4_0[2]), .in_3(A_4_0[1]), .in_4(A_4_0[0]),
    .in_5(A_4_0[4]), .in_6(A_4_0[3]), .in_7(A_4_0[2]), .in_8(A_4_0[1]), .in_9(A_4_0[0]), .in_10(A_4_0[4]),
    .in_11(A_4_0[3]), .in_12(A_4_0[2]), .in_13(A_4_0[1]), .in_14(A_4_0[0]), .in_15(A_4_0[4]),
    .in_16(A_4_0[3]), .in_17(A_4_0[2]), .in_18(A_4_0[1]), .in_19(A_4_0[0]), .in_20(A_4_0[4]),
    .in_21(A_4_0[3]), .in_22(A_4_0[2]), .in_23(A_4_0[1]), .in_24(A_4_0[0]), .in_25(A_4_0[4]),
    .in_26(A_4_0[3]), .in_27(A_4_0[2]), .in_28(A_4_0[1]), .in_29(A_4_0[0]), .in_30(A_4_0[4]),
    .in_31(A_4_0[3]), .out(R_4_0[4]));
  Multiplexer #(.Selector_Bits(5)) multiplexer_2 (
    .sel(B_4_0), .in_0(A_4_0[3]), .in_1(A_4_0[2]), .in_2(A_4_0[1]), .in_3(A_4_0[0]), .in_4(A_4_0[4]),
    .in_5(A_4_0[3]), .in_6(A_4_0[2]), .in_7(A_4_0[1]), .in_8(A_4_0[0]), .in_9(A_4_0[4]), .in_10(A_4_0[3]),
    .in_11(A_4_0[2]), .in_12(A_4_0[1]), .in_13(A_4_0[0]), .in_14(A_4_0[4]), .in_15(A_4_0[3]),
    .in_16(A_4_0[2]), .in_17(A_4_0[1]), .in_18(A_4_0[0]), .in_19(A_4_0[4]), .in_20(A_4_0[3]),
    .in_21(A_4_0[2]), .in_22(A_4_0[1]), .in_23(A_4_0[0]), .in_24(A_4_0[4]), .in_25(A_4_0[3]),
    .in_26(A_4_0[2]), .in_27(A_4_0[1]), .in_28(A_4_0[0]), .in_29(A_4_0[4]), .in_30(A_4_0[3]),
    .in_31(A_4_0[2]), .out(R_4_0[3]));
  Multiplexer #(.Selector_Bits(5)) multiplexer_3 (
    .sel(B_4_0), .in_0(A_4_0[2]), .in_1(A_4_0[1]), .in_2(A_4_0[0]), .in_3(A_4_0[4]), .in_4(A_4_0[3]),
    .in_5(A_4_0[2]), .in_6(A_4_0[1]), .in_7(A_4_0[0]), .in_8(A_4_0[4]), .in_9(A_4_0[3]), .in_10(A_4_0[2]),
    .in_11(A_4_0[1]), .in_12(A_4_0[0]), .in_13(A_4_0[4]), .in_14(A_4_0[3]), .in_15(A_4_0[2]),
    .in_16(A_4_0[1]), .in_17(A_4_0[0]), .in_18(A_4_0[4]), .in_19(A_4_0[3]), .in_20(A_4_0[2]),
    .in_21(A_4_0[1]), .in_22(A_4_0[0]), .in_23(A_4_0[4]), .in_24(A_4_0[3]), .in_25(A_4_0[2]),
    .in_26(A_4_0[1]), .in_27(A_4_0[0]), .in_28(A_4_0[4]), .in_29(A_4_0[3]), .in_30(A_4_0[2]),
    .in_31(A_4_0[1]), .out(R_4_0[2]));
  Multiplexer #(.Selector_Bits(5)) multiplexer_4 (
    .sel(B_4_0), .in_0(A_4_0[1]), .in_1(A_4_0[0]), .in_2(A_4_0[4]), .in_3(A_4_0[3]), .in_4(A_4_0[2]),
    .in_5(A_4_0[1]), .in_6(A_4_0[0]), .in_7(A_4_0[4]), .in_8(A_4_0[3]), .in_9(A_4_0[2]), .in_10(A_4_0[1]),
    .in_11(A_4_0[0]), .in_12(A_4_0[4]), .in_13(A_4_0[3]), .in_14(A_4_0[2]), .in_15(A_4_0[1]),
    .in_16(A_4_0[0]), .in_17(A_4_0[4]), .in_18(A_4_0[3]), .in_19(A_4_0[2]), .in_20(A_4_0[1]),
    .in_21(A_4_0[0]), .in_22(A_4_0[4]), .in_23(A_4_0[3]), .in_24(A_4_0[2]), .in_25(A_4_0[1]),
    .in_26(A_4_0[0]), .in_27(A_4_0[4]), .in_28(A_4_0[3]), .in_29(A_4_0[2]), .in_30(A_4_0[1]),
    .in_31(A_4_0[0]), .out(R_4_0[1]));
  Multiplexer #(.Selector_Bits(5)) multiplexer_5 (
    .sel(B_4_0), .in_0(A_4_0[0]), .in_1(A_4_0[4]), .in_2(A_4_0[3]), .in_3(A_4_0[2]), .in_4(A_4_0[1]),
    .in_5(A_4_0[0]), .in_6(A_4_0[4]), .in_7(A_4_0[3]), .in_8(A_4_0[2]), .in_9(A_4_0[1]), .in_10(A_4_0[0]),
    .in_11(A_4_0[4]), .in_12(A_4_0[3]), .in_13(A_4_0[2]), .in_14(A_4_0[1]), .in_15(A_4_0[0]),
    .in_16(A_4_0[4]), .in_17(A_4_0[3]), .in_18(A_4_0[2]), .in_19(A_4_0[1]), .in_20(A_4_0[0]),
    .in_21(A_4_0[4]), .in_22(A_4_0[3]), .in_23(A_4_0[2]), .in_24(A_4_0[1]), .in_25(A_4_0[0]),
    .in_26(A_4_0[4]), .in_27(A_4_0[3]), .in_28(A_4_0[2]), .in_29(A_4_0[1]), .in_30(A_4_0[0]),
    .in_31(A_4_0[4]), .out(R_4_0[0]));

  // Other names for the same wires on the sheet: A0 = A_4_0[0]; A1 = A_4_0[1]; A2 = A_4_0[2]; A3 = A_4_0[3];
  //   A4 = A_4_0[4]; R0 = R_4_0[0]; R1 = R_4_0[1]; R2 = R_4_0[2]; R3 = R_4_0[3]; R4 = R_4_0[4]; Sel[4:0] = B_4_0
endmodule
