// Digital circuit 5 bit Reg.dig as structural Verilog
module _5_bit_Reg (
  input  [4:0] Din_4_0,
  input  Sel,
  input  CLK,
  output [4:0] Dout
);

  _1_bit_Reg _1_bit_reg_1 (.Din(Din_4_0[4]), .Sel(Sel), .CLK(CLK), .Dout(Dout[4]));
  _1_bit_Reg _1_bit_reg_2 (.Din(Din_4_0[3]), .Sel(Sel), .CLK(CLK), .Dout(Dout[3]));
  _1_bit_Reg _1_bit_reg_3 (.Din(Din_4_0[2]), .Sel(Sel), .CLK(CLK), .Dout(Dout[2]));
  _1_bit_Reg _1_bit_reg_4 (.Din(Din_4_0[1]), .Sel(Sel), .CLK(CLK), .Dout(Dout[1]));
  _1_bit_Reg _1_bit_reg_5 (.Din(Din_4_0[0]), .Sel(Sel), .CLK(CLK), .Dout(Dout[0]));

  // Other names for the same wires on the sheet: I0 = Din_4_0[0]; I1 = Din_4_0[1]; I2 = Din_4_0[2]; I3 = Din_4_0[3];
  //   I4 = Din_4_0[4]; O0 = Dout[0]; O1 = Dout[1]; O2 = Dout[2]; O3 = Dout[3]; O4 = Dout[4]
endmodule
