// Digital circuit 5 bit XOR.dig as structural Verilog
module _5_bit_XOR (
  input  [4:0] A_4_0,
  input  [4:0] B_4_0,
  output [4:0] R_4_0
);

  xor xor_1 (R_4_0[0], A_4_0[0], B_4_0[0]);
  xor xor_2 (R_4_0[1], A_4_0[1], B_4_0[1]);
  xor xor_3 (R_4_0[2], A_4_0[2], B_4_0[2]);
  xor xor_4 (R_4_0[3], A_4_0[3], B_4_0[3]);
  xor xor_5 (R_4_0[4], A_4_0[4], B_4_0[4]);

  // Other names for the same wires on the sheet: A0 = A_4_0[0]; A1 = A_4_0[1]; A2 = A_4_0[2]; A3 = A_4_0[3];
  //   A4 = A_4_0[4]; B0 = B_4_0[0]; B1 = B_4_0[1]; B2 = B_4_0[2]; B3 = B_4_0[3]; B4 = B_4_0[4]; R0 = R_4_0[0];
  //   R1 = R_4_0[1]; R2 = R_4_0[2]; R3 = R_4_0[3]; R4 = R_4_0[4]
endmodule
