// Digital circuit CPU.dig as structural Verilog
module CPU (
  input  [2:0] WR_3_0,
  input  [14:0] WRD_14_0,
  input  WE,
  input  CLK,
  input  PC_EN,
  input  [2:0] RA2_2_0,
  input  SF,
  input  ZF,
  output [14:0] RD2_14_0,
  output [1:0] WR_1_0,
  output [1:0] R1_1_0,
  output [1:0] R2_1_0,
  output [4:0] A_4_0,
  output [4:0] B_4_0,
  output [4:0] R_4_0,
  output [2:0] JMP_ADDR
);

  wire CPU_CLK, IMM_SEL, JMP_SEL, REG_EN;
  wire [1:0] OP;
  wire [2:0] _3_bit_pc_adder_1_o_2_0, _3_bit_program_counter_1_o_2_0, multiplexer_1_out;
  wire [4:0] _3x5_reg_set_1_b_4_0;
  wire [6:0] XX;
  wire [14:11] _7x15_ram_1_rd1_14_0;

  Multiplexer #(.Bits(3)) multiplexer_1 (
    .sel(JMP_SEL), .in_0(_3_bit_pc_adder_1_o_2_0), .in_1(JMP_ADDR), .out(multiplexer_1_out));
  _3_bit_PC_Adder _3_bit_pc_adder_1 (.I_2_0(_3_bit_program_counter_1_o_2_0), .O_2_0(_3_bit_pc_adder_1_o_2_0));
  _3_bit_Program_Counter _3_bit_program_counter_1 (
    .I_2_0(multiplexer_1_out), .CLK(CPU_CLK), .O_2_0(_3_bit_program_counter_1_o_2_0));
  and and_1 (CPU_CLK, PC_EN, CLK);
  _7x15_RAM _7x15_ram_1 (
    .RA1_2_0(_3_bit_program_counter_1_o_2_0), .RA2_2_0(RA2_2_0), .WR_2_0(WR_3_0), .WRD_14_0(WRD_14_0),
    .WE(WE), .CLK(CLK), .RD1_14_0({_7x15_ram_1_rd1_14_0, JMP_ADDR, R2_1_0[0], XX}), .RD2_14_0(RD2_14_0));
  _3x5_Reg_Set _3x5_reg_set_1 (
    .REG_EN(REG_EN), .WRD_4_0(R_4_0), .WR_1_0(JMP_ADDR[2:1]), .CLK(CPU_CLK), .Ra_1_0(JMP_ADDR[2:1]),
    .Rb_1_0({JMP_ADDR[0], R2_1_0[0]}), .A_4_0(A_4_0), .B_4_0(_3x5_reg_set_1_b_4_0));
  _5_bit_ALU _5_bit_alu_1 (.A_4_0(A_4_0), .B_4_0(B_4_0), .OP_1_0(OP), .R_4_0(R_4_0));
  Control_Unit control_unit_1 (
    .Opcode_3_0(_7x15_ram_1_rd1_14_0), .SF(SF), .ZF(ZF), .OP_1_0(OP), .REG_EN(REG_EN), .Imm_Sel(IMM_SEL),
    .JMP_Sel(JMP_SEL));
  Multiplexer #(.Bits(5)) multiplexer_2 (
    .sel(IMM_SEL), .in_0(_3x5_reg_set_1_b_4_0), .in_1({JMP_ADDR[0], R2_1_0[0], XX[6:4]}), .out(B_4_0));

  assign R1_1_0 = JMP_ADDR[2:1];
  assign R2_1_0[1] = JMP_ADDR[0];
  assign WR_1_0 = JMP_ADDR[2:1];

  // Other names for the same wires on the sheet: R2[1:0] = {JMP_ADDR[0], R2_1_0[0]}; R1[1:0] = JMP_ADDR[2:1];
  //   A[4:0] = A_4_0; B[4:0] = B_4_0; R[4:0] = R_4_0; RA2[2:0] = RA2_2_0; RD2[14:0] = RD2_14_0

  // Notes on the sheet:
  //   Register Mode: 2 bit (op type=00) + 2 bit(op) + 2 bit (reg1) + 2 bit (reg2) + 7 bit (x)
  //   Immediate Mode: 2 bit (op type=01) + 2 bit(op) + 2 bit (reg1) + 5 bit (value) + 4 bit (x)
  //   Branching Mode: 2 bit (op type=10) + 2 bit(op) + 3 bit (addr) + 8 bit (x)
  //   XOR (op = 00), ADD (op = 01), ROL (op = 10)
  //   JMP (op = 00), JLE (op = 01)
  //   START:
  //       XOR R1, R1 -->  000001010000000
  //       JLE 0     -->	  100100000000000
  //   LABEL:
  //       ADD R1, 2 -->  010101000100000
  //       JMP LABEL -->  100001000000000
endmodule
