// Digital circuit Full Adder.dig as structural Verilog
module Full_Adder (
  input  X,
  input  Y,
  input  Cin,
  output Cout,
  output S
);

  wire and_1_out, and_2_out, xor_1_out;

  xor xor_1 (xor_1_out, X, Y);
  and and_1 (and_1_out, Y, X);
  and and_2 (and_2_out, Cin, xor_1_out);
  xor xor_2 (S, xor_1_out, Cin);
  or or_1 (Cout, and_2_out, and_1_out);

  // Other names for the same wires on the sheet: Sum = S
endmodule
